# Fritzing sketch agriWatering (saved by Fritzing 0.9.3b)
breadboards: 1

parts:
  パーツ1 = Arduino Uno (Rev3)
  M1 = DC Motor
  T1 = LM35 Temperature Sensor [package="TO92 [THT]"]
  Q1 = NPN-Transistor [package="TO92 [THT]"]
  パーツ3 = Soil Moisture Sensor

nets:
  N1: パーツ1.A0, T1.Vout
  N2: パーツ1.A1, パーツ3.SIG
  N3: パーツ1.D13/SCK, Q1.B
  GND: パーツ1.GND, M1.pin_2, T1.GND, パーツ3.GND
  3V3: パーツ1.3V3, T1.+Vs, パーツ3.VCC
  N4: パーツ1.5V, Q1.C
  N5: M1.pin_1, Q1.E

notes:
  agriWatering
